# Fritzing sketch Float_Sensor (saved by Fritzing 0.9.10b)

parts:
  U1 = ESP 32 DEVKIT DOIT
  M1 = water level switch

nets:
  N1: U1.D22, U1.D18, U1.3V3, M1.pin1
  N2: U1.GND, M1.pin2

custom parts:
  water level switch: Generic water level float switch.
